# Fritzing sketch 01_DHT11 (saved by Fritzing 0.9.3b)
breadboards: 1

parts:
  WeMos_D1_Mini1 = WeMos D1 Mini
  DHT1 = DHT11 Humitidy and Temperature Sensor
  R1 = Resistor [tolerance=±5% resistance=10k package="1206 [SMD]"]

nets:
  5V: WeMos_D1_Mini1.5V, DHT1.VDD, R1.Pin_0
  N1: WeMos_D1_Mini1.D2, DHT1.DATA, R1.Pin_1
  N2: WeMos_D1_Mini1.G, DHT1.GND

custom parts:
  DHT11 Humitidy and Temperature Sensor: DHT11 Humidity and Temperature Sensor
