# Fritzing sketch 02_light_analog (saved by Fritzing 0.9.3b)
breadboards: 1

parts:
  R1 = Resistor [tolerance=±5% resistance=10k package="1206 [SMD]"]
  WeMos_D1_Mini1 = WeMos D1 Mini
  R2 = Photocell (LDR) [package=THT]
  R3 = Resistor [tolerance=±5% resistance=1k package="0805 [SMD]"]
  D1 = LTE-302 [package=lte-302]

nets:
  N1: R1.Pin_0, WeMos_D1_Mini1.G, D1.C
  N2: R1.Pin_1, R2.pin_0
  N3: WeMos_D1_Mini1.3V3, R2.pin_1
  N4: WeMos_D1_Mini1.D2, R3.Pin_0
  N5: R3.Pin_1, D1.A
