# Fritzing sketch 04_rgb_led (saved by Fritzing 0.9.3b)
breadboards: 1

parts:
  WeMos_D1_Mini1 = WeMos D1 Mini
  R1 = Resistor [tolerance=±5% resistance=1k package=THT]
  C1 = Electrolytic Capacitor [capacitance=10µF voltage=10V package="100 mil [THT, electrolytic]"]
  Часть1 = ws2812b [package="smd 2812b"]

nets:
  5V: WeMos_D1_Mini1.5V, C1.+, Часть1.VDD
  N1: WeMos_D1_Mini1.D2, R1.Pin_0
  N2: WeMos_D1_Mini1.G, C1.-, Часть1.VSS
  N3: R1.Pin_1, Часть1.DIN
