# Fritzing sketch 06_blinds (saved by Fritzing 0.9.3b)
breadboards: 1

parts:
  WeMos_D1_Mini1 = WeMos D1 Mini
  J1 = Basic Servo

nets:
  5V: WeMos_D1_Mini1.5V, J1.vcc
  N1: WeMos_D1_Mini1.D2, J1.pulse
  N2: WeMos_D1_Mini1.G, J1.gnd
